// Digital circuit decoder.dig as structural Verilog
module decoder (
  input  [1:0] S,
  output A_1,
  output A_2,
  output A_3,
  output A_4
);

  Decoder #(.Selector_Bits(2)) decoder_1 (.sel(S), .out_0(A_1), .out_1(A_2), .out_2(A_3), .out_3(A_4));
endmodule
