// Digital circuit decoder_xor.dig as structural Verilog
module decoder_xor (
  input  A,
  input  B,
  output Y
);

  wire decoder_1_out_1, decoder_1_out_2;

  Decoder #(.Selector_Bits(2)) decoder_1 (
    .sel({B, A}), .out_1(decoder_1_out_1), .out_2(decoder_1_out_2));  // open: out_0, out_3
  or or_1 (Y, decoder_1_out_1, decoder_1_out_2);

  // Notes on the sheet:
  //   We can build logic gates using a decoder.
  //   Each decoder output represents a single SOP term (more proper terminology is "minterm").
  //   So, we can OR together SOP terms to build any logic function. For example, this is a 2-input XOR gate.
endmodule

/* Test case:
A B Y
0 0 0
0 1 1
1 0 1
1 1 0
*/
