// Digital circuit encoder.dig as structural Verilog
module encoder (
  input  A_3,
  input  A_2,
  input  A_4,
  output S_1,
  output S_2
);

  or or_1 (S_1, A_2, A_4);
  or or_2 (S_2, A_3, A_4);
endmodule
