// Digital circuit ex_decoder_nand.dig as structural Verilog
module ex_decoder_nand (
  input  A,
  input  B,
  output Y
);

  Decoder #(.Selector_Bits(2)) decoder_1 (.sel({B, A}));  // open: out_0, out_1, out_2, out_3
  // Or or_1 has open pins: In_1=open, In_2=open, In_3=open, out=Y

  // Notes on the sheet:
  //   Make a 2-input NAND gate using this 2:4 decoder
  //   and a 3-input OR gate by adding wire(s).
  //   Run tests to verify your work.
endmodule

/* Test case:
A B Y
0 0 1
0 1 1
1 0 1
1 1 0
*/
