// Digital circuit ex_decoder_or.dig as structural Verilog
module ex_decoder_or (
  input  A,
  input  B,
  output Y
);

  Decoder #(.Selector_Bits(2)) decoder_1 (.sel({B, A}));  // open: out_0, out_1, out_2, out_3
  // Or or_1 has open pins: In_1=open, In_2=open, In_3=open, out=Y

  // Notes on the sheet:
  //   Make an OR gate using this 2:4 decoder by adding wire(s).
  //   Run tests to verify your work.
  //   Optionally, make other logic gates (e.g., AND, XNOR, etc.).
endmodule

/* Test case:
A B Y
0 0 0
0 1 1
1 0 1
1 1 1
*/
