// Digital circuit ex_mux_4_to_1.dig as structural Verilog
module ex_mux_4_to_1 (
  input  A,
  input  B,
  input  C,
  input  D,
  input  S_2,
  input  S_1,
  output Y
);

  wire multiplexer_1_out, multiplexer_2_out;

  Multiplexer multiplexer_1 (.in_0(A), .in_1(B), .out(multiplexer_1_out));  // open: sel
  Multiplexer multiplexer_2 (.in_0(C), .in_1(D), .out(multiplexer_2_out));  // open: sel
  Multiplexer multiplexer_3 (.in_0(multiplexer_1_out), .in_1(multiplexer_2_out), .out(Y));  // open: sel

  // Notes on the sheet:
  //   Create a 4:1 MUX using only 2:1 MUX.
  //   To see how a 4:1 MUX works, see mux\_4\_to\_1.dig,
  //   and you can see the truth table by right clicking the green Test box
  //   and clicking "Edit".
  //   Some parts of the circuit are given to you.
  //   You need only add wires from S_2 and S_1.
  //   To check your work, press the triangular button
  //   with a green checkmark at the top.
endmodule

/* Test case:
S_2 S_1 A B C D Y
0 0 0 0 0 0 0
0 0 0 0 0 1 0
0 0 0 0 1 0 0
0 0 0 0 1 1 0
0 0 0 1 0 0 0
0 0 0 1 0 1 0
0 0 0 1 1 0 0
0 0 0 1 1 1 0
0 0 1 0 0 0 1
0 0 1 0 0 1 1 
0 0 1 0 1 0 1
0 0 1 0 1 1 1
0 0 1 1 0 0 1
0 0 1 1 0 1 1
0 0 1 1 1 0 1
0 0 1 1 1 1 1
0 1 0 0 0 0 0
0 1 0 0 0 1 0 
0 1 0 0 1 0 0
0 1 0 0 1 1 0
0 1 0 1 0 0 1
0 1 0 1 0 1 1
0 1 0 1 1 0 1
0 1 0 1 1 1 1
0 1 1 0 0 0 0
0 1 1 0 0 1 0
0 1 1 0 1 0 0
0 1 1 0 1 1 0
0 1 1 1 0 0 1
0 1 1 1 0 1 1
0 1 1 1 1 0 1
0 1 1 1 1 1 1
1 0 0 0 0 0 0
1 0 0 0 0 1 0
1 0 0 0 1 0 1
1 0 0 0 1 1 1
1 0 0 1 0 0 0
1 0 0 1 0 1 0
1 0 0 1 1 0 1
1 0 0 1 1 1 1
1 0 1 0 0 0 0
1 0 1 0 0 1 0
1 0 1 0 1 0 1
1 0 1 0 1 1 1
1 0 1 1 0 0 0
1 0 1 1 0 1 0
1 0 1 1 1 0 1
1 0 1 1 1 1 1
1 1 0 0 0 0 0
1 1 0 0 0 1 1
1 1 0 0 1 0 0
1 1 0 0 1 1 1
1 1 0 1 0 0 0
1 1 0 1 0 1 1
1 1 0 1 1 0 0
1 1 0 1 1 1 1
1 1 1 0 0 0 0
1 1 1 0 0 1 1
1 1 1 0 1 0 0
1 1 1 0 1 1 1
1 1 1 1 0 0 0
1 1 1 1 0 1 1
1 1 1 1 1 0 0
1 1 1 1 1 1 1
*/
