// Digital circuit ex_mux_xor.dig as structural Verilog
module ex_mux_xor (
  input  A,
  input  B,
  output Y
);

  Multiplexer #(.Selector_Bits(2)) multiplexer_1 (.sel({B, A}), .out(Y));  // open: in_0, in_1, in_2, in_3

  // Notes on the sheet:
  //   Create a 2-input XOR gate using a 4:1 MUX.
  //   You need only add wire(s).
  //   To check your work, press the triangular button
  //   with a green checkmark at the top.
endmodule

/* Test case:
A B Y
0 0 0
0 1 1
1 0 1
1 1 0
*/
