// Digital circuit mux_4_to_1.dig as structural Verilog
module mux_4_to_1 (
  input  [1:0] S,
  input  A,
  input  B,
  input  C,
  input  D,
  output Y
);

  Multiplexer #(.Selector_Bits(2)) multiplexer_1 (.sel(S), .in_0(A), .in_1(B), .in_2(C), .in_3(D), .out(Y));
endmodule

/* Test case:
S A B C D Y
0 0 0 0 0 0
0 0 0 0 1 0
0 0 0 1 0 0
0 0 0 1 1 0
0 0 1 0 0 0
0 0 1 0 1 0
0 0 1 1 0 0
0 0 1 1 1 0
0 1 0 0 0 1
0 1 0 0 1 1 
0 1 0 1 0 1
0 1 0 1 1 1
0 1 1 0 0 1
0 1 1 0 1 1
0 1 1 1 0 1
0 1 1 1 1 1
1 0 0 0 0 0
1 0 0 0 1 0 
1 0 0 1 0 0
1 0 0 1 1 0
1 0 1 0 0 1
1 0 1 0 1 1
1 0 1 1 0 1
1 0 1 1 1 1
1 1 0 0 0 0
1 1 0 0 1 0
1 1 0 1 0 0
1 1 0 1 1 0
1 1 1 0 0 1
1 1 1 0 1 1
1 1 1 1 0 1
1 1 1 1 1 1
2 0 0 0 0 0
2 0 0 0 1 0
2 0 0 1 0 1
2 0 0 1 1 1
2 0 1 0 0 0
2 0 1 0 1 0
2 0 1 1 0 1
2 0 1 1 1 1
2 1 0 0 0 0
2 1 0 0 1 0
2 1 0 1 0 1
2 1 0 1 1 1
2 1 1 0 0 0
2 1 1 0 1 0
2 1 1 1 0 1
2 1 1 1 1 1
3 0 0 0 0 0
3 0 0 0 1 1
3 0 0 1 0 0
3 0 0 1 1 1
3 0 1 0 0 0
3 0 1 0 1 1
3 0 1 1 0 0
3 0 1 1 1 1
3 1 0 0 0 0
3 1 0 0 1 1
3 1 0 1 0 0
3 1 0 1 1 1
3 1 1 0 0 0
3 1 1 0 1 1
3 1 1 1 0 0
3 1 1 1 1 1
*/
